# Fritzing sketch the-sensor-project (saved by Fritzing 0.9.4)
breadboards: 1

parts:
  Componente1 = Barometric Pressure Sensor - BMP180 Breakout (GY-68)
  Raspberry_Pi_B_rev1 = Raspberry Pi B rev1
  R1 = Resistor [tolerance=±0.5% resistance=180 package="0402 [SMD]"]
  R2 = Resistor [tolerance=±0.5% resistance=180 package="0402 [SMD]"]
  R3 = Resistor [tolerance=±0.5% resistance=180 package="0402 [SMD]"]
  LED1 = LED - 5mm [color="Red (633nm)" package="5 mm [THT]"]
  LED3 = LED - 5mm [color="Green (555nm)" package="5 mm [THT]"]
  LED2 = smd LED [color="Yellow (595nm)" package="0603 [SMD]"]
  LED2_2 = LED - 3mm [color="Yellow (595nm)" package="3 mm [THT]"]
  R4 = Photocell (LDR) [package=THT]
  C2 = Capacitor Polarized [package=panasonic_c]
  Sensore_PIR_HC-SR502 = HC-SR501 Body Sensor Module

nets:
  VCC: Componente1.VCC, Raspberry_Pi_B_rev1.3V3, R4.pin_1, C2.-, Sensore_PIR_HC-SR502.VCC
  GND: Componente1.GND, Raspberry_Pi_B_rev1.GND, Sensore_PIR_HC-SR502.GND
  N1: Componente1.SCL, Raspberry_Pi_B_rev1.GPIO_1
  N2: Componente1.SDA, Raspberry_Pi_B_rev1.GPIO_0
  N3: Raspberry_Pi_B_rev1.GPIO_23, R3.Pin_1
  N4: Raspberry_Pi_B_rev1.GPIO_4, R4.pin_0
  N5: Raspberry_Pi_B_rev1.GPIO_24, R2.Pin_1
  N6: Raspberry_Pi_B_rev1.GPIO_25, R1.Pin_1
  N7: R1.Pin_0, LED1.anode
  N8: R2.Pin_0, LED2.anode, LED2_2.anode
  N9: R3.Pin_0, LED3.anode
  N10: LED1.cathode, LED3.cathode, LED2.cathode, LED2_2.cathode

custom parts:
  HC-SR501 Body Sensor Module: Pyroelectric Infrared PIR Motion Sensor Detector Module
